// Logisim project ALU_FETCH.circ as structural Verilog
module ALU (
  input  [7:0] A,
  input  [7:0] B,
  input  [5:0] Opcode,
  output Sign_Flag,
  output [7:0] out_5,
  output Zero_Flag,
  output Carry_Flag
);

  wire adder_1_carry_out, adder_2_carry_out, adder_3_carry_out, adder_4_carry_out, adder_5_carry_out,
       adder_6_carry_out, adder_7_carry_out;

  Adder adder_1 (
    .INVA(Opcode[1]), .A(A[7]), .ENA(Opcode[3]), .B(B[7]), .ENB(Opcode[2]), .Carry_in(Opcode[0]),
    .F0(Opcode[5]), .F1(Opcode[4]), .Carry_out(adder_1_carry_out), .Output(out_5[7]));
  Adder adder_2 (
    .INVA(Opcode[1]), .A(A[6]), .ENA(Opcode[3]), .B(B[6]), .ENB(Opcode[2]), .Carry_in(adder_1_carry_out),
    .F0(Opcode[5]), .F1(Opcode[4]), .Carry_out(adder_2_carry_out), .Output(out_5[6]));
  Adder adder_3 (
    .INVA(Opcode[1]), .A(A[5]), .ENA(Opcode[3]), .B(B[5]), .ENB(Opcode[2]), .Carry_in(adder_2_carry_out),
    .F0(Opcode[5]), .F1(Opcode[4]), .Carry_out(adder_3_carry_out), .Output(out_5[5]));
  Adder adder_4 (
    .INVA(Opcode[1]), .A(A[4]), .ENA(Opcode[3]), .B(B[4]), .ENB(Opcode[2]), .Carry_in(adder_3_carry_out),
    .F0(Opcode[5]), .F1(Opcode[4]), .Carry_out(adder_4_carry_out), .Output(out_5[4]));
  Adder adder_5 (
    .INVA(Opcode[1]), .A(A[3]), .ENA(Opcode[3]), .B(B[3]), .ENB(Opcode[2]), .Carry_in(adder_4_carry_out),
    .F0(Opcode[5]), .F1(Opcode[4]), .Carry_out(adder_5_carry_out), .Output(out_5[3]));
  Adder adder_6 (
    .INVA(Opcode[1]), .A(A[2]), .ENA(Opcode[3]), .B(B[2]), .ENB(Opcode[2]), .Carry_in(adder_5_carry_out),
    .F0(Opcode[5]), .F1(Opcode[4]), .Carry_out(adder_6_carry_out), .Output(out_5[2]));
  Adder adder_7 (
    .INVA(Opcode[1]), .A(A[1]), .ENA(Opcode[3]), .B(B[1]), .ENB(Opcode[2]), .Carry_in(adder_6_carry_out),
    .F0(Opcode[5]), .F1(Opcode[4]), .Carry_out(adder_7_carry_out), .Output(out_5[1]));
  Adder adder_8 (
    .INVA(Opcode[1]), .A(A[0]), .ENA(Opcode[3]), .B(B[0]), .ENB(Opcode[2]), .Carry_in(adder_7_carry_out),
    .F0(Opcode[5]), .F1(Opcode[4]), .Carry_out(Carry_Flag), .Output(out_5[0]));
  nor nor_1 (Zero_Flag, out_5[7], out_5[6], out_5[5], out_5[4], out_5[3], out_5[2], out_5[1], out_5[0]);

  assign Sign_Flag = out_5[7];

  // Notes on the sheet:
  //   Lab 8
  //   Jacob, Christoss, Graham
endmodule

module Adder (
  input  INVA,
  input  A,
  input  ENA,
  input  B,
  input  ENB,
  input  Carry_in,
  input  F0,
  input  F1,
  output Output,
  output Carry_out
);

  wire A_out, and_1_out, and_2_out, and_3_out, and_4_out, and_5_out, and_6_out, B_out, C_out, D_out,
       hold_1_bit_1_sum, not_1_out, not_2_out, not_3_out, not_4_out, not_5_out, or_1_out, xor_1_out;

  not not_1 (not_1_out, F0);
  xor xor_1 (xor_1_out, INVA, and_1_out);
  and and_1 (and_1_out, A, ENA);
  and and_2 (and_2_out, B, ENB);
  not not_2 (not_2_out, F1);
  not not_3 (not_3_out, F0);
  not not_4 (not_4_out, F1);
  and u_A (A_out, not_1_out, not_2_out);
  and u_B (B_out, not_3_out, F1);
  and C (C_out, F0, not_4_out);
  and D (D_out, F0, F1);
  and and_3 (and_3_out, xor_1_out, and_2_out);
  or or_1 (or_1_out, xor_1_out, and_2_out);
  not not_5 (not_5_out, and_2_out);
  and and_4 (and_4_out, and_3_out, A_out);
  and and_5 (and_5_out, or_1_out, B_out);
  and and_6 (and_6_out, not_5_out, C_out);
  hold_1_bit hold_1_bit_1 (
    .Carry_in(Carry_in), .A(and_2_out), .B(xor_1_out), .in_4(D_out), .Carry_out(Carry_out),
    .Sum(hold_1_bit_1_sum));
  or or_2 (Output, and_4_out, and_5_out, and_6_out, hold_1_bit_1_sum);

  // Notes on the sheet:
  //   AB
  //   A+B
  //   Not B
  //   Sum
endmodule

module hold_1_bit (
  input  Carry_in,
  input  A,
  input  B,
  input  in_4,
  output Sum,
  output Carry_out
);

  wire and_1_out, and_2_out, xor_1_out, xor_2_out;

  and and_1 (and_1_out, in_4, B, A);
  xor xor_1 (xor_1_out, A, B);
  or or_1 (Carry_out, and_1_out, and_2_out);
  and and_2 (and_2_out, in_4, Carry_in, xor_1_out);
  xor xor_2 (xor_2_out, Carry_in, xor_1_out);
  and and_3 (Sum, xor_2_out, in_4);
endmodule

module fetch (
  input  Clock,
  input  Load_Data,
  input  in_3,
  input  Enable,
  input  Clock_2,
  input  Clear,
  output [7:0] Current_Addr,
  output [15:0] Data_out_bus,
  output [7:0] _8_bit_inst,
  output [7:0] _8_bit_imm_value,
  output [1:0] out_11,
  output [5:0] Opcode,
  output [1:0] out_13,
  output [7:0] out_14,
  output [7:0] out_15,
  output [7:0] out_16,
  output [7:0] out_17,
  output [7:0] out_18,
  output out_19,
  output out_20,
  output out_21,
  output [7:0] out_22,
  output [7:0] out_23,
  output [7:0] out_24,
  output [7:0] out_25
);

  Control_Store control_store_1 (
    .Source(out_13), .Destination(out_11), .Instruction(_8_bit_inst), .Immediate(_8_bit_imm_value),
    .Opcode(Opcode), .ImmOut(out_14));
  PC_IR pc_ir_1 (
    .Clear(Clear), .Enable(Enable), .Clock(Clock_2), .instruction(_8_bit_inst), .addr_out(Current_Addr),
    .data_in(Data_out_bus), .immediate_value(_8_bit_imm_value));
  Register_File register_file_1 (
    .Data_in(out_17), .in_4(Enable), .Data_out_0(out_15), .Data_out_1(out_18), .in_2(out_11),
    .Clock(Clock_2), .SR_0(out_13), .SR_1(out_11), .Clear(Clear), .R3(out_25), .R2(out_24), .R0(out_22),
    .R1(out_23));
  Multiplexer #(.width(8)) multiplexer_1 (.in0(out_14), .in1(out_15), .out(out_16), .sel(in_3), .en(Enable));
  RAM #(.dataWidth(16)) ram_1 (
    .addr(Current_Addr), .data(Data_out_bus), .sel(Enable), .clk(Clock), .ld(Load_Data), .clr(Clear));
  ALU alu_1 (
    .A(out_16), .B(out_18), .Opcode(Opcode), .out_5(out_17), .Carry_Flag(out_21), .Sign_Flag(out_19),
    .Zero_Flag(out_20));

  // Other names for the same wires on the sheet: Clock_t = Clock_2; R0[7:0] = out_22; R1[7:0] = out_23;
  //   R2[7:0] = out_24; R3[7:0] = out_25

  // Notes on the sheet:
  //   Load RAM with program
  //   Enable the PC_IR chip
  //   Each time you clock 0-->1-->0
  //   Next instruction is loaded 
  //   1 = no imm
  //   0 = use imm
  //   Note: data can flow either direction - in or out of RAM
  //   We only need data flowing out of RAM
  //   Turn on Chip Select and Load Data
  //   Do Not Clock, it's used to move data into RAM
endmodule

module PC_IR (
  input  Clear,
  input  Enable,
  input  Clock,
  input  [15:0] data_in,
  output [7:0] addr_out,
  output [7:0] instruction,
  output [7:0] immediate_value
);

  wire [7:0] adder_1_out;

  Register PC (.D(adder_1_out), .en(Enable), .Q(addr_out), .clk(Clock), .clr(Clear));
  Register #(.width(16)) IR (.D(data_in), .en(Enable), .Q({instruction, immediate_value}), .clk(Clock), .clr(Clear));
  Adder_part adder_1 (.a(8'h1), .b(addr_out), .out(adder_1_out), .cin(1'b0));  // open: cout
endmodule

module Register_File (
  input  [1:0] SR_0,
  input  [1:0] in_2,
  input  [7:0] Data_in,
  input  in_4,
  input  Clock,
  input  Clear,
  input  [1:0] SR_1,
  output [7:0] R0,
  output [7:0] R1,
  output [7:0] Data_out_0,
  output [7:0] Data_out_1,
  output [7:0] R3,
  output [7:0] R2
);

  wire demultiplexer_1_out0, demultiplexer_1_out1, demultiplexer_1_out2, demultiplexer_1_out3;
  wire [7:0] Register__2_q;

  Demultiplexer #(.select(2)) demultiplexer_1 (
    .out0(demultiplexer_1_out0), .out1(demultiplexer_1_out1), .out2(demultiplexer_1_out2),
    .out3(demultiplexer_1_out3), .in(in_4), .sel(in_2), .en(in_4));
  Register Register__0 (.D(Data_in), .en(demultiplexer_1_out0), .Q(R0), .clk(Clock), .clr(Clear));
  Register Register__1 (.D(Data_in), .en(demultiplexer_1_out1), .Q(R1), .clk(Clock), .clr(Clear));
  Register Register__2 (.D(Data_in), .en(demultiplexer_1_out2), .Q(Register__2_q), .clk(Clock), .clr(Clear));
  Register Register__3 (.D(Data_in), .en(demultiplexer_1_out3), .Q(R2), .clk(Clock), .clr(Clear));
  Multiplexer #(.select(2), .width(8)) multiplexer_1 (
    .in0(R0), .in1(R1), .in2(Register__2_q), .in3(R2), .out(Data_out_0), .sel(SR_0), .en(in_4));
  Multiplexer #(.select(2), .width(8)) multiplexer_2 (
    .in0(R0), .in1(R1), .in2(Register__2_q), .in3(R2), .out(Data_out_1), .sel(SR_1), .en(in_4));

  assign R3 = R2;

  // Other names for the same wires on the sheet: Enable = in_4
endmodule
